# Fritzing sketch DoomSlayerShoulderCannonProject (saved by Fritzing 1.0.6)
breadboards: 1

parts:
  V1 = Pulse Power [voltage=5V amplitude=0 period=20ms number_of_pulses=0 offset_voltage=5V delay_time=0s internal_resistance=0.1Ω]
  Part1 = Arduino Uno (Rev3)
  J1 = Basic Servo
  J2 = Basic Servo

nets:
  VCC: V1.V+, J1.vcc, J2.vcc
  GND: V1.V-, J1.gnd, J2.gnd
  N1: Part1.D2, J1.pulse
  N2: Part1.D3_PWM, J2.pulse
